# Fritzing sketch Ard_PS (saved by Fritzing 0.9.0b)
breadboards: 2

parts:
  부품1 = Arduino Uno (Rev3)
  부품2 = Bluetooth Mate Silver
  부품3 = Barometric Pressure Sensor - BMP085 Breakout
  R2 = Resistor [tolerance=±5% resistance=220 package=THT]
  부품4 = Arduino Uno (Rev3)
  부품5 = Bluetooth Mate Silver

nets:
  N1: 부품1.A0, 부품3.EOC, R2.Pin_0
  N2: 부품1.D12/MISO, 부품2.VCC
  N3: 부품1.D13/SCK, 부품2.CTS_5V
  N4: 부품2.RX_5V, R2.Pin_1
  N5: 부품2.TX_5V, 부품3.XCLR
  N6: 부품4.D12/MISO, 부품5.VCC
  N7: 부품4.D13/SCK, 부품5.CTS_5V
